# Fritzing sketch Connection (saved by Fritzing 0.9.2b)

parts:
  U1 = NodeMCU V1.0
  DHT1 = DHT22 Humidity and Temperature Sensor
  Grove1 = Grove OLED 128x96
  JP1 = USB_MICROB_PLUG [package=micro-b-th]
  LED1 = LED - 5mm [color="Red (633nm)" package="5 mm [THT]"]
  R1 = Resistor [tolerance=±5% resistance=1k package=THT]
  R2 = Resistor [tolerance=±5% resistance=150 package=THT]  # not connected
  R3 = Resistor [tolerance=±5% resistance=1k package=THT]  # not connected
  C1 = Electrolytic Capacitor [capacitance=220µF package="100 mil [THT, electrolytic]"]
  R4 = Resistor [tolerance=±5% resistance=220k package=THT]
  U2 = Sharp Dust Sensor [part_number=GP2Y1010AU0F]

nets:
  N1: U1.D1, Grove1.SCL
  N2: U1.D2, Grove1.SDA
  3V3: U1.3V3, DHT1.VDD
  GND: U1.GND, DHT1.GND, JP1.GND
  N3: U1.D5, R1.Pin_1
  N4: U1.D6, U2.LED
  N5: U1.D7, DHT1.DATA
  N6: U1.Vin, JP1.D+
  N7: U1.A0, R4.Pin_1
  N8: LED1.cathode, R1.Pin_0
  N9: C1.-, U2.LED-GND
  N10: C1.+, U2.V-LED
  N11: R4.Pin_0, U2.Vo

custom parts:
  NodeMCU V1.0: ESP8266 based NodeMCU
  Sharp Dust Sensor: Sharp GP2Y1010AU0F Dust Sensor
