# Fritzing sketch OLED_DHT22 (saved by Fritzing 0.9.2b)

parts:
  U1 = NodeMCU V1.0
  Grove1 = Grove OLED 128x96
  DHT1 = DHT22 Humidity and Temperature Sensor

nets:
  N1: U1.D1, Grove1.SCL
  N2: U1.D2, Grove1.SDA
  3V3: U1.3V3, Grove1.VCC, DHT1.VDD
  GND: U1.GND, Grove1.GND, DHT1.GND
  N3: U1.D7, DHT1.DATA

custom parts:
  NodeMCU V1.0: ESP8266 based NodeMCU
