# Fritzing sketch connection (saved by Fritzing 0.9.2b)
breadboards: 1

parts:
  U1 = NodeMCU V1.0
  DHT1 = DHT11 Humitidy and Temperature Sensor
  R1 = Resistor [tolerance=±5% resistance=1k package=THT]
  LED1 = smd LED [color="Red (633nm)" package="1206 [SMD]"]
  R2 = Resistor [tolerance=±5% resistance=1k package=THT]
  S1 = Momentary Switch [package=ksa_sealed_tac_switch]
  R3 = Resistor [tolerance=±5% resistance=1k package=THT]

nets:
  N1: U1.D1, DHT1.DATA, R1.Pin_1
  N2: U1.D2, R2.Pin_0
  N3: U1.D3, S1.4, R3.Pin_1
  3V3: U1.3V3, DHT1.VDD, R1.Pin_0, S1.2
  GND: U1.GND, DHT1.GND, LED1.cathode, R3.Pin_0
  N4: LED1.anode, R2.Pin_1

custom parts:
  NodeMCU V1.0: ESP8266 based NodeMCU
  DHT11 Humitidy and Temperature Sensor: DHT11 Humidity and Temperature Sensor
